// Logisim project Adder_using_NOR.circ as structural Verilog: 1 circuit, main circuit main
module main (
  input  A,
  input  B,
  input  Cin,
  output Sum
);

  wire nor_1_out, nor_2_out, nor_3_out, nor_4_out, nor_5_out, nor_6_out, nor_7_out, nor_8_out, nor_9_out;

  nor nor_1 (nor_1_out, B, A);
  nor nor_2 (nor_2_out, B, nor_1_out);
  nor nor_3 (nor_3_out, nor_1_out, A);
  nor nor_4 (nor_4_out, nor_2_out, nor_3_out);
  nor nor_5 (nor_5_out, nor_4_out, nor_4_out);
  nor nor_6 (nor_6_out, nor_5_out, Cin);
  nor nor_7 (nor_7_out, nor_5_out, nor_6_out);
  nor nor_8 (nor_8_out, nor_6_out, Cin);
  nor nor_9 (nor_9_out, nor_7_out, nor_8_out);
  nor nor_10 (Sum, nor_9_out, nor_9_out);
endmodule
