// Logisim project Arithmatic_Unit.circ as structural Verilog: 1 circuit, main circuit main
// 8
module main (
  input  [1:0] in_1,
  input  [7:0] in_2,
  input  [7:0] in_3,
  input  in_4,
  output out_5,
  output out_6,
  output out_7,
  output out_8,
  output out_9,
  output out_10,
  output out_11,
  output out_12,
  output out_13,
  output out_14
);

  wire adder_1_cout, adder_1_out, adder_2_cout, adder_2_out, adder_3_cout, adder_3_out, adder_4_cout,
       adder_4_out, adder_5_cout, adder_5_out, adder_6_cout, adder_6_out, adder_7_cout, adder_7_out,
       adder_8_cout, adder_8_out, and_1_out, and_2_out, and_3_out, and_4_out, and_5_out, and_6_out,
       and_7_out, and_8_out, and_9_out, and_10_out, and_11_out, and_12_out, and_13_out, and_14_out,
       and_15_out, and_16_out, not_1_out, not_2_out, not_3_out, not_4_out, not_5_out, not_6_out, not_7_out,
       not_8_out, or_1_out, or_2_out, or_3_out, or_5_out, or_6_out, or_7_out, or_8_out;

  not not_1 (not_1_out, in_3[7]);
  and and_1 (and_1_out, not_1_out, in_1[1]);
  and and_2 (and_2_out, in_1[0], in_3[7]);
  or or_1 (or_1_out, and_1_out, and_2_out);
  not not_2 (not_2_out, in_3[6]);
  and and_3 (and_3_out, not_2_out, in_1[1]);
  Adder #(.width(1)) adder_1 (.a(or_1_out), .b(in_2[7]), .out(adder_1_out), .cin(adder_2_cout), .cout(adder_1_cout));
  assign out_13 = out_14 ? adder_1_cout : 1'bz;  // Controlled_Buffer controlled_buffer_1
  and and_4 (and_4_out, in_1[0], in_3[6]);
  or or_2 (or_2_out, and_3_out, and_4_out);
  not not_3 (not_3_out, in_3[5]);
  and and_5 (and_5_out, not_3_out, in_1[1]);
  or or_3 (or_3_out, and_5_out, and_6_out);
  Adder #(.width(1)) adder_2 (.a(or_2_out), .b(in_2[6]), .out(adder_2_out), .cin(adder_3_cout), .cout(adder_2_cout));
  assign out_12 = out_14 ? adder_1_out : 1'bz;  // Controlled_Buffer controlled_buffer_2
  and and_6 (and_6_out, in_1[0], in_3[5]);
  Adder #(.width(1)) adder_3 (.a(or_3_out), .b(in_2[5]), .out(adder_3_out), .cin(adder_4_cout), .cout(adder_3_cout));
  assign out_9 = out_14 ? adder_2_out : 1'bz;  // Controlled_Buffer controlled_buffer_3
  not not_4 (not_4_out, in_3[4]);
  and and_7 (and_7_out, not_4_out, in_1[1]);
  or or_4 (in_2[5], and_7_out, and_8_out);
  and and_8 (and_8_out, in_1[0], in_3[4]);
  Adder #(.width(1)) adder_4 (.a(in_2[5]), .b(in_2[4]), .out(adder_4_out), .cin(adder_5_cout), .cout(adder_4_cout));
  not not_5 (not_5_out, in_3[3]);
  and and_9 (and_9_out, not_5_out, in_1[1]);
  or or_5 (or_5_out, and_9_out, and_10_out);
  assign out_10 = out_14 ? adder_3_out : 1'bz;  // Controlled_Buffer controlled_buffer_4
  and and_10 (and_10_out, in_1[0], in_3[3]);
  Adder #(.width(1)) adder_5 (.a(or_5_out), .b(in_2[3]), .out(adder_5_out), .cin(adder_6_cout), .cout(adder_5_cout));
  assign out_11 = out_14 ? adder_4_out : 1'bz;  // Controlled_Buffer controlled_buffer_5
  not not_6 (not_6_out, in_3[2]);
  and and_11 (and_11_out, not_6_out, in_1[1]);
  or or_6 (or_6_out, and_11_out, and_12_out);
  and and_12 (and_12_out, in_1[0], in_3[2]);
  Adder #(.width(1)) adder_6 (.a(or_6_out), .b(in_2[2]), .out(adder_6_out), .cin(adder_7_cout), .cout(adder_6_cout));
  not not_7 (not_7_out, in_3[1]);
  assign out_6 = out_14 ? adder_5_out : 1'bz;  // Controlled_Buffer controlled_buffer_6
  and and_13 (and_13_out, not_7_out, in_1[1]);
  or or_7 (or_7_out, and_13_out, and_14_out);
  and and_14 (and_14_out, in_1[0], in_3[1]);
  Adder #(.width(1)) adder_7 (.a(or_7_out), .b(in_2[1]), .out(adder_7_out), .cin(adder_8_cout), .cout(adder_7_cout));
  assign out_7 = out_14 ? adder_6_out : 1'bz;  // Controlled_Buffer controlled_buffer_7
  not not_8 (not_8_out, in_3[0]);
  and and_15 (and_15_out, not_8_out, in_1[1]);
  and and_16 (and_16_out, in_1[0], in_3[0]);
  or or_8 (or_8_out, and_15_out, and_16_out);
  Adder #(.width(1)) adder_8 (.a(or_8_out), .b(in_2[0]), .out(adder_8_out), .cin(in_4), .cout(adder_8_cout));
  assign out_8 = out_14 ? adder_7_out : 1'bz;  // Controlled_Buffer controlled_buffer_8
  assign out_5 = out_14 ? adder_8_out : 1'bz;  // Controlled_Buffer controlled_buffer_9
endmodule
