// Logisim project ArrayMult.circ as structural Verilog: 1 circuit, main circuit main
module main (
  input  [3:0] B0B1B2B3,
  input  [3:0] A3A2A1A0,
  input  Carry_In,
  input  in_4,
  output [7:0] Product
);

  wire adder_2_cout, adder_2_out, adder_3_cout, adder_3_out, adder_4_cout, adder_5_cout, adder_5_out,
       adder_6_cout, adder_6_out, adder_7_cout, adder_8_cout, adder_8_out, adder_9_cout, adder_9_out,
       adder_10_cout, adder_11_cout, adder_12_cout, B0A1_out, B0A2_out, B0A3_out, B1A0_out, B1A1_out,
       B1A2_out, B1A3_out, B2A0_out, B2A1_out, B2A2_out, B2A3_out, B3A0_out, B3A1_out, B3A2_out, B3A3_out;

  and B3A3 (B3A3_out, A3A2A1A0[3], B0B1B2B3[3]);
  Adder #(.width(1)) adder_1 (.a(B3A3_out), .b(adder_2_cout), .out(Product[6]), .cin(adder_4_cout), .cout(Product[7]));
  and B2A3 (B2A3_out, A3A2A1A0[3], B0B1B2B3[2]);
  Adder #(.width(1)) adder_2 (
    .a(B2A3_out), .b(adder_3_cout), .out(adder_2_out), .cin(adder_6_cout), .cout(adder_2_cout));
  and B1A3 (B1A3_out, A3A2A1A0[3], B0B1B2B3[1]);
  Adder #(.width(1)) adder_3 (.a(B1A3_out), .b(in_4), .out(adder_3_out), .cin(adder_5_cout), .cout(adder_3_cout));
  and B3A2 (B3A2_out, A3A2A1A0[2], B0B1B2B3[3]);
  Adder #(.width(1)) adder_4 (.a(adder_2_out), .b(B3A2_out), .out(Product[5]), .cin(adder_7_cout), .cout(adder_4_cout));
  and B0A3 (B0A3_out, A3A2A1A0[3], B0B1B2B3[0]);
  and B1A2 (B1A2_out, A3A2A1A0[2], B0B1B2B3[1]);
  Adder #(.width(1)) adder_5 (.a(B1A2_out), .b(B0A3_out), .out(adder_5_out), .cin(adder_9_cout), .cout(adder_5_cout));
  and B2A2 (B2A2_out, A3A2A1A0[2], B0B1B2B3[2]);
  Adder #(.width(1)) adder_6 (
    .a(adder_3_out), .b(B2A2_out), .out(adder_6_out), .cin(adder_8_cout), .cout(adder_6_cout));
  and B0A2 (B0A2_out, A3A2A1A0[2], B0B1B2B3[0]);
  and B2A1 (B2A1_out, A3A2A1A0[1], B0B1B2B3[2]);
  and B3A1 (B3A1_out, A3A2A1A0[1], B0B1B2B3[3]);
  Adder #(.width(1)) adder_7 (
    .a(adder_6_out), .b(B3A1_out), .out(Product[4]), .cin(adder_10_cout), .cout(adder_7_cout));
  and B1A1 (B1A1_out, A3A2A1A0[1], B0B1B2B3[1]);
  Adder #(.width(1)) adder_8 (
    .a(adder_5_out), .b(B2A1_out), .out(adder_8_out), .cin(adder_12_cout), .cout(adder_8_cout));
  and B3A0 (B3A0_out, A3A2A1A0[0], B0B1B2B3[3]);
  and B0A1 (B0A1_out, A3A2A1A0[1], B0B1B2B3[0]);
  Adder #(.width(1)) adder_9 (.a(B1A1_out), .b(B0A2_out), .out(adder_9_out), .cin(adder_11_cout), .cout(adder_9_cout));
  and B2A0 (B2A0_out, A3A2A1A0[0], B0B1B2B3[2]);
  Adder #(.width(1)) adder_10 (.a(adder_8_out), .b(B3A0_out), .out(Product[3]), .cin(Carry_In), .cout(adder_10_cout));
  and B1A0 (B1A0_out, A3A2A1A0[0], B0B1B2B3[1]);
  Adder #(.width(1)) adder_11 (.a(B1A0_out), .b(B0A1_out), .out(Product[1]), .cin(Carry_In), .cout(adder_11_cout));
  Adder #(.width(1)) adder_12 (.a(adder_9_out), .b(B2A0_out), .out(Product[2]), .cin(Carry_In), .cout(adder_12_cout));
  and B0A0 (Product[0], A3A2A1A0[0], B0B1B2B3[0]);

  // Notes on the sheet:
  //   Multiplicand
  //   Multiplier
endmodule
