// Logisim project FullAdder.circ as structural Verilog: 1 circuit, main circuit main
module main (
  input  A,
  input  B,
  input  Cin,
  output Sum,
  output Cout
);

  wire and_1_out, and_2_out, AxorB_out;

  xor AxorB (AxorB_out, B, A);
  xor xor_1 (Sum, AxorB_out, Cin);
  and and_1 (and_1_out, AxorB_out, Cin);
  and and_2 (and_2_out, A, B);
  or or_1 (Cout, and_1_out, and_2_out);
endmodule
