// Logisim project LogicUnit.circ as structural Verilog: 1 circuit, main circuit main
module main (
  input  [7:0] in_1,
  input  [7:0] in_2,
  input  [1:0] in_3,
  input  in_4,
  output out_5,
  output out_6,
  output out_7,
  output out_8,
  output out_9,
  output out_10,
  output out_11,
  output out_12
);

  wire and_1_out, and_2_out, and_3_out, and_4_out, and_5_out, and_6_out, and_7_out, and_8_out,
       multiplexer_1_out, multiplexer_2_out, multiplexer_3_out, multiplexer_4_out, multiplexer_5_out,
       multiplexer_6_out, multiplexer_7_out, multiplexer_8_out, not_1_out, not_2_out, not_3_out, not_4_out,
       not_5_out, not_6_out, not_7_out, not_8_out, or_1_out, or_2_out, or_3_out, or_4_out, or_5_out,
       or_6_out, or_7_out, or_8_out, xor_1_out, xor_2_out, xor_3_out, xor_4_out, xor_5_out, xor_6_out,
       xor_7_out, xor_8_out;

  or or_1 (or_1_out, in_1[7], in_2[7]);
  or or_2 (or_2_out, in_1[6], in_2[6]);
  buf or_3 (or_3_out, in_1[5]);  // OR_Gate
  or or_4 (or_4_out, in_1[4], in_2[5]);
  or or_5 (or_5_out, in_1[3], in_2[4]);
  Multiplexer #(.select(2)) multiplexer_1 (
    .in0(or_1_out), .in1(and_1_out), .in2(xor_1_out), .in3(not_1_out), .out(multiplexer_1_out), .sel(in_3));
  or or_6 (or_6_out, in_1[2], in_2[3]);
  assign out_5 = in_4 ? multiplexer_1_out : 1'bz;  // Controlled_Buffer controlled_buffer_1
  or or_7 (or_7_out, in_1[1], in_2[1]);
  or or_8 (or_8_out, in_1[0], in_2[0]);
  Multiplexer #(.select(2)) multiplexer_2 (
    .in0(or_2_out), .in1(and_2_out), .in2(xor_2_out), .in3(not_2_out), .out(multiplexer_2_out), .sel(in_3));
  assign out_6 = in_4 ? multiplexer_2_out : 1'bz;  // Controlled_Buffer controlled_buffer_2
  and and_1 (and_1_out, in_1[0], in_2[7]);
  and and_2 (and_2_out, in_1[1], in_2[6]);
  and and_3 (and_3_out, in_1[2], in_2[5]);
  Multiplexer #(.select(2)) multiplexer_3 (
    .in0(or_3_out), .in1(and_3_out), .in2(xor_3_out), .in3(not_3_out), .out(multiplexer_3_out), .sel(in_3));
  assign out_7 = in_4 ? multiplexer_3_out : 1'bz;  // Controlled_Buffer controlled_buffer_3
  and and_4 (and_4_out, in_1[3], in_2[4]);
  and and_5 (and_5_out, in_1[4], in_2[3]);
  and and_6 (and_6_out, in_1[5], in_2[2]);
  Multiplexer #(.select(2)) multiplexer_4 (
    .in0(or_4_out), .in1(and_4_out), .in2(xor_4_out), .in3(not_4_out), .out(multiplexer_4_out), .sel(in_3));
  assign out_8 = in_4 ? multiplexer_4_out : 1'bz;  // Controlled_Buffer controlled_buffer_4
  and and_7 (and_7_out, in_1[6], in_2[1]);
  and and_8 (and_8_out, in_1[7], in_2[0]);
  xor xor_1 (xor_1_out, in_1[7], in_2[7]);
  xor xor_2 (xor_2_out, in_1[6], in_2[6]);
  xor xor_3 (xor_3_out, in_1[5], in_2[5]);
  xor xor_4 (xor_4_out, in_1[4], in_2[4]);
  Multiplexer #(.select(2)) multiplexer_5 (
    .in0(or_5_out), .in1(and_5_out), .in2(xor_5_out), .in3(not_5_out), .out(multiplexer_5_out), .sel(in_3));
  assign out_9 = in_4 ? multiplexer_5_out : 1'bz;  // Controlled_Buffer controlled_buffer_5
  xor xor_5 (xor_5_out, in_1[3], in_2[3]);
  xor xor_6 (xor_6_out, in_1[2], in_2[2]);
  xor xor_7 (xor_7_out, in_1[1], in_2[1]);
  Multiplexer #(.select(2)) multiplexer_6 (
    .in0(or_6_out), .in1(and_6_out), .in2(xor_6_out), .in3(not_6_out), .out(multiplexer_6_out), .sel(in_3));
  assign out_10 = in_4 ? multiplexer_6_out : 1'bz;  // Controlled_Buffer controlled_buffer_6
  xor xor_8 (xor_8_out, in_1[0], in_2[0]);
  Multiplexer #(.select(2)) multiplexer_7 (
    .in0(or_7_out), .in1(and_7_out), .in2(xor_7_out), .in3(not_7_out), .out(multiplexer_7_out), .sel(in_3));
  assign out_11 = in_4 ? multiplexer_7_out : 1'bz;  // Controlled_Buffer controlled_buffer_7
  not not_1 (not_1_out, in_2[7]);
  not not_2 (not_2_out, in_2[6]);
  not not_3 (not_3_out, in_2[5]);
  not not_4 (not_4_out, in_2[4]);
  not not_5 (not_5_out, in_2[3]);
  not not_6 (not_6_out, in_2[2]);
  not not_7 (not_7_out, in_2[1]);
  Multiplexer #(.select(2)) multiplexer_8 (
    .in0(or_8_out), .in1(and_8_out), .in2(xor_8_out), .in3(not_8_out), .out(multiplexer_8_out), .sel(in_3));
  assign out_12 = in_4 ? multiplexer_8_out : 1'bz;  // Controlled_Buffer controlled_buffer_8
  not not_8 (not_8_out, in_2[0]);
endmodule
